# Fritzing sketch flight-computer (saved by Fritzing 0.9.3b)

parts:
  Part1 = Adafruit Feather M0 Adalogger [part_number="Adafruit #2796"]
  Part2 = Adafruit FXOS8700 + FXAS21002 9 DoF Breakout [part_number="Adafruit #3463"]
  Part3 = Adafruit_BMP280
  Part4 = Adafruit Ultimate GPS v3 [part_number="Adafruit #746"]
  J1 = Basic Servo
  J2 = Basic Servo
  VCC1_11_7v = Battery
  BEC_(part_of_ESC) = Voltage Regulator - 5V [package="TO220 [THT]"]

nets:
  GND: Part1.GND, Part2.GND, Part3.GND, Part4.GND, J1.gnd, J2.gnd, VCC1_11_7v.+, BEC_(part_of_ESC).GND
  N1: Part1.D1, Part4.TX
  N2: Part1.D0, Part4.RX
  VIN: Part1.+3V3, Part2.VIN, Part4.VIN
  VCC: Part1.VBAT, J1.vcc, J2.vcc, BEC_(part_of_ESC).output_voltage
  N3: Part1.D12, Part3.SDO/ADR
  N4: Part1.D11, Part3.SDI/SDA
  N5: Part1.D10, Part3.SCK/SCL
  N6: Part1.D9, Part3.CS
  N7: Part1.D6, J1.pulse
  N8: Part1.D5, J2.pulse
  N9: Part1.SCL, Part2.SCL
  N10: Part1.SDA, Part2.SDA
  N11: VCC1_11_7v.-, BEC_(part_of_ESC).input_voltage

custom parts:
  Adafruit Feather M0 Adalogger: This is the Adafruit Feather M0 Adalogger - our take on an 'all-in-one' Cortex M0 datalogger (or data-reader) with built in USB and battery charging. Its an Adafruit Feather M0 with a microSD holder ready to rock! We have other boards in the Feather family, check'em out here At the Feather M0's heart is an ATSAMD21G18 ARM Cortex M0 processor, clocked at 48 MHz and at 3.3V logic, the same one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
  Adafruit FXOS8700 + FXAS21002 9 DoF Breakout: The NXP Precision 9DoF breakout combines two of the best motion sensors we've tested here at Adafruit: The FXOS8700 3-Axis accelerometer and magnetometer, and the FXAS21002 3-axis gyroscope. These two sensors combine to make a nice 9-DoF kit, that can be used for motion and orientation sensing. In particular, we think this sensor set is ideal for AHRS-based orientation calculations: the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
  Adafruit_BMP280: Bosch has stepped up their game with their new BMP280 sensor, an environmental sensor with temperature, barometric pressure that is the next generation upgrade to the BMP085/BMP180/BMP183. This sensor is great for all sorts of weather sensing and can even be used in both I2C and SPI! This precision sensor from Bosch is the best low-cost, precision sensing solution for measuring barometric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
  Adafruit Ultimate GPS v3: We carry a few different GPS modules here in the Adafruit shop, but none that satisfied our every desire - that's why we designed this little GPS breakout board. We believe this is the Ultimate GPS module, so we named it that. It's got everything you want and more: -165 dBm sensitivity, 10 Hz updates, 66 channels 5V friendly design and only 20mA current draw Breadboard friendly + two mounting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
